// Logisim project D8421Convert.circ as structural Verilog: 1 circuit, main circuit main
module main (
  input  [3:0] D8421,
  output [3:0] D8421___4,
  output E,
  output F,
  output G,
  output H
);

  wire and_1_out, and_2_out, and_3_out, and_4_out, and_5_out, and_6_out, and_7_out, not_1_out, not_2_out,
       not_3_out, not_4_out;

  // Probe on D8421
  not not_1 (not_1_out, D8421[0]);
  not not_2 (not_2_out, D8421[1]);
  not not_3 (not_3_out, D8421[2]);
  not not_4 (not_4_out, D8421[3]);
  and and_1 (and_1_out, not_4_out, D8421[2]);
  and and_2 (and_2_out, D8421[3], not_3_out, not_2_out);
  and and_3 (and_3_out, not_4_out, not_3_out);
  and and_4 (and_4_out, not_3_out, not_2_out);
  and and_5 (and_5_out, not_4_out, D8421[1]);
  and and_6 (and_6_out, not_4_out, D8421[0]);
  and and_7 (and_7_out, not_3_out, D8421[0], not_2_out);
  or or_1 (D8421___4[3], and_1_out, and_2_out);
  or or_2 (D8421___4[2], and_3_out, and_4_out);
  buf or_3 (D8421___4[1], and_5_out);  // OR_Gate
  or or_4 (D8421___4[0], and_6_out, and_7_out);
  // Probe on D8421___4

  assign E = D8421___4[3];
  assign F = D8421___4[2];
  assign G = D8421___4[1];
  assign H = D8421___4[0];

  // Notes on the sheet:
  //   A
  //   C
  //   D
  //   B
  //   !A
  //   !B
  //   !C
  //   !D
endmodule
