// Logisim project SUMM.circ as structural Verilog: 1 circuit, main circuit main
module main (
  input  V
);

  wire clock_1_out, nand_1_out, nand_2_out, nand_3_out, nand_4_out, nand_5_out, nand_6_out, nand_7_out,
       nand_8_out, nand_9_out, nand_10_out;
  wire [2:0] I_q;

  // Probe on I_q
  nand nand_1 (nand_1_out, I_q[0], I_q[0]);
  nand nand_2 (nand_2_out, I_q[1], I_q[1]);
  T_Flip_Flop J (.clk(clock_1_out), .T(nand_9_out), .Q(I_q[2]));  // open: Qn, preset, reset
  T_Flip_Flop H (.clk(clock_1_out), .T(nand_10_out), .Q(I_q[1]));  // open: Qn, preset, reset
  T_Flip_Flop I (.clk(clock_1_out), .T(V), .Q(I_q[0]));  // open: Qn, preset, reset
  Clock clock_1 (.out(clock_1_out));
  nand nand_3 (nand_3_out, nand_1_out, nand_1_out);
  nand nand_4 (nand_4_out, nand_2_out, nand_2_out);
  nand nand_5 (nand_5_out, V, nand_3_out, nand_4_out);
  nand nand_6 (nand_6_out, V, nand_3_out, nand_4_out);
  nand nand_7 (nand_7_out, nand_3_out, V);
  nand nand_8 (nand_8_out, V, nand_3_out);
  nand nand_9 (nand_9_out, nand_5_out, nand_6_out);
  nand nand_10 (nand_10_out, nand_7_out, nand_8_out);

  // Notes on the sheet:
  //   C
  //   A
  //   B
  //   !B
  //   !A
  //   B
  //   A
endmodule
